// Logisim project RV32IM.circ as structural Verilog: 4 circuits, main circuit main
module CPU (
  input  [31:0] mem_read_data,
  input  [31:0] inst,
  input  clk,
  output [31:0] mem_addr,
  output [31:0] mem_write_data,
  output mem_w_en,
  output [31:0] PC,
  output [31:0] reg_gp
);

  wire and_1_out, and_2_out, and_3_out, and_4_out, and_5_out, and_6_out, B_beq, B_bge, B_bgeu, B_blt, B_bltu,
       B_bne, B_type, comparator_1_eq, comparator_2_eq, comparator_3_lt, comparator_4_lt, comparator_5_lt,
       comparator_6_lt, comparator_16_eq, comparator_17_eq, comparator_18_eq, comparator_19_eq,
       comparator_20_eq, comparator_21_eq, comparator_22_eq, comparator_23_eq, comparator_24_eq,
       comparator_25_eq, comparator_26_eq, comparator_27_eq, comparator_28_eq, comparator_29_eq,
       comparator_30_eq, comparator_31_eq, comparator_32_eq, comparator_33_eq, comparator_34_eq,
       comparator_35_eq, comparator_36_eq, comparator_37_eq, comparator_38_eq, comparator_39_eq,
       comparator_40_eq, comparator_41_eq, comparator_42_eq, comparator_43_eq, comparator_44_eq,
       comparator_45_eq, comparator_46_eq, comparator_47_eq, comparator_48_eq, comparator_49_eq,
       comparator_50_eq, comparator_51_eq, comparator_52_eq, comparator_53_eq, comparator_54_eq,
       comparator_55_eq, comparator_56_eq, comparator_57_eq, comparator_58_eq, comparator_59_eq,
       comparator_60_eq, comparator_61_eq, comparator_62_eq, comparator_63_eq, I_add, I_and, I_jalr, I_lb,
       I_lh, I_lw, I_or, I_sll, I_slt, I_srl, I_type, I_type_arith, I_type_load, I_xor, J_type, or_1_out,
       or_2_out, or_3_out, or_4_out, or_5_out, or_6_out, or_10_out, or_11_out, or_12_out, or_13_out,
       or_14_out, or_15_out, or_16_out, or_17_out, R_add, R_and, R_div, R_mul, R_mulh, R_or, R_rem, R_sll,
       R_slt, R_srl, R_sub, R_type, R_xor, reg_w_en, S_sw, U_lui, U_type, U_type_AUIPC;
  wire [1:0] priority_encoder_1_out, priority_encoder_2_out, priority_encoder_3_out;
  wire [2:0] priority_encoder_5_out;
  wire [3:0] priority_encoder_4_out;
  wire [31:0] bit_extender_1_out, bit_extender_2_out, bit_extender_3_out, bit_extender_4_out, imm_value,
       multiplexer_1_out, multiplexer_2_out, multiplexer_3_out, multiplexer_4_out, PC_plus_4, r1_data;

  // Probe on inst
  Comparator #(.width(32)) comparator_1 (.a(r1_data), .b(mem_write_data), .eq(comparator_1_eq));  // open: gt, lt
  Comparator #(.width(32)) comparator_2 (.a(r1_data), .b(mem_write_data), .eq(comparator_2_eq));  // open: gt, lt
  Comparator #(.width(32)) comparator_3 (.a(r1_data), .b(mem_write_data), .lt(comparator_3_lt));  // open: gt, eq
  Comparator #(.width(32)) comparator_4 (.a(r1_data), .b(mem_write_data), .lt(comparator_4_lt));  // open: gt, eq
  Comparator #(.mode("unsigned"), .width(32)) comparator_5 (
    .a(r1_data), .b(mem_write_data), .lt(comparator_5_lt));  // open: gt, eq
  Comparator #(.mode("unsigned"), .width(32)) comparator_6 (
    .a(r1_data), .b(mem_write_data), .lt(comparator_6_lt));  // open: gt, eq
  or or_1 (or_1_out, R_type, I_type_arith, U_lui);
  or or_2 (or_2_out, J_type, I_jalr);
  or or_3 (or_3_out, R_type, I_type, mem_w_en);
  or or_4 (or_4_out, B_type, J_type);
  or or_5 (or_5_out, I_type, mem_w_en, B_type, U_type, J_type);
  and and_1 (and_1_out, B_beq, comparator_1_eq);
  and and_2 (and_2_out, B_bne, ~comparator_2_eq);  // AND_Gate
  and and_3 (and_3_out, B_blt, comparator_3_lt);
  and and_4 (and_4_out, B_bge, ~comparator_4_lt);  // AND_Gate
  and and_5 (and_5_out, B_bltu, comparator_5_lt);
  and and_6 (and_6_out, B_bgeu, ~comparator_6_lt);  // AND_Gate
  or or_6 (or_6_out, I_jalr, J_type);
  or or_7 (reg_w_en, R_type, I_type, U_type, J_type);
  Priority_Encoder #(.select(2)) priority_encoder_1 (
    .in0(I_type_load), .in1(or_1_out), .in2(or_2_out), .out(priority_encoder_1_out));  // open: in3, gs, en_out, en_in
  Priority_Encoder #(.select(2)) priority_encoder_2 (
    .in0(or_3_out), .in1(or_4_out), .in2(U_lui), .out(priority_encoder_2_out));  // open: in3, gs, en_out, en_in
  Priority_Encoder #(.select(2)) priority_encoder_3 (
    .in0(R_type), .in1(or_5_out), .out(priority_encoder_3_out));  // open: in2, in3, gs, en_out, en_in
  Adder #(.width(32)) adder_1 (.a(PC), .b(32'h4), .out(PC_plus_4));  // open: cin, cout
  or or_8 (I_type, I_type_arith, I_type_load, I_jalr);
  or or_9 (U_type, U_lui, U_type_AUIPC);
  Multiplexer #(.select(2), .width(32)) multiplexer_1 (
    .in0(mem_read_data), .in1(mem_addr), .in2(PC_plus_4), .out(multiplexer_1_out),
    .sel(priority_encoder_1_out));  // open: in3
  or or_10 (or_10_out, R_slt, I_slt);
  Multiplexer #(.width(32)) multiplexer_2 (.in0(PC_plus_4), .in1(mem_addr), .out(multiplexer_2_out), .sel(or_11_out));
  or or_11 (or_11_out, and_1_out, and_2_out, and_3_out, and_4_out, and_5_out, and_6_out, or_6_out);
  assign bit_extender_1_out = {{20{inst[31]}}, inst[31:20]};  // Bit_Extender bit_extender_1
  assign bit_extender_2_out = {{20{inst[31]}}, {inst[31:25], inst[11:7]}};  // Bit_Extender bit_extender_2
  assign bit_extender_3_out = {{19{inst[31]}}, {inst[31], inst[7], inst[30:25], inst[11:8], 1'b0}};  // Bit_Extender bit_extender_3
  assign bit_extender_4_out = {{11{inst[31]}}, {inst[31], inst[19:12], inst[20], inst[30:21], 1'b0}};  // Bit_Extender bit_extender_4
  RegFile regfile_1 (
    .reg_w_en(reg_w_en), .clk(clk), .reg_read_idx1(inst[19:15]), .reg_read_idx2(inst[24:20]),
    .reg_w_idx(inst[11:7]), .reg_write_data(multiplexer_1_out), .RegReadData1(r1_data),
    .RegReadData2(mem_write_data), .reg_gp(reg_gp));
  Multiplexer #(.select(2), .width(32)) multiplexer_3 (
    .in0(mem_write_data), .in1(imm_value), .in2({32{1'b0}}), .out(multiplexer_3_out),
    .sel(priority_encoder_3_out));  // open: in3
  or or_12 (or_12_out, R_add, I_add);
  or or_13 (or_13_out, R_and, I_and);
  or or_14 (or_14_out, R_or, I_or);
  or or_15 (or_15_out, R_xor, I_xor);
  or or_16 (or_16_out, R_sll, I_sll);
  or or_17 (or_17_out, R_srl, I_srl);
  Register #(.width(32)) register_1 (.D(multiplexer_2_out), .en(clk), .clk(clk), .Q(PC));  // open: clr
  Multiplexer #(.select(2), .width(32)) multiplexer_4 (
    .in0(r1_data), .in1(PC), .in2({32{1'b0}}), .out(multiplexer_4_out), .sel(priority_encoder_2_out));  // open: in3
  Priority_Encoder #(.select(4)) priority_encoder_4 (
    .in0(or_12_out), .in1(R_sub), .in2(or_13_out), .in3(or_14_out), .in4(or_15_out), .in5(or_16_out),
    .in6(or_17_out), .in7(R_mul), .in8(R_mulh), .in9(R_div), .in10(R_rem), .in11(or_10_out),
    .out(priority_encoder_4_out));  // open: in12, in13, in14, in15, gs, en_out, en_in
  Multiplexer #(.select(3), .width(32)) multiplexer_5 (
    .in0(bit_extender_1_out), .in1(bit_extender_2_out), .in2(bit_extender_3_out),
    .in3({inst[31:12], {12{1'b0}}}), .in4(bit_extender_4_out), .out(imm_value), .sel(priority_encoder_5_out));  // open: in5, in6, in7
  Priority_Encoder priority_encoder_5 (
    .in0(I_type), .in1(mem_w_en), .in2(B_type), .in3(U_type), .in4(J_type), .out(priority_encoder_5_out));  // open: in5, in6, in7, en_in, gs, en_out
  ALU alu_1 (.A(multiplexer_4_out), .B(multiplexer_3_out), .OP(priority_encoder_4_out), .C(mem_addr));
  Comparator #(.width(7)) comparator_7 (.a(inst[6:0]), .b(7'b0110011), .eq(R_type));  // open: gt, lt
  Comparator #(.width(7)) comparator_8 (.a(inst[6:0]), .b(7'b0010011), .eq(I_type_arith));  // open: gt, lt
  Comparator #(.width(7)) comparator_9 (.a(inst[6:0]), .b(7'b0000011), .eq(I_type_load));  // open: gt, lt
  Comparator #(.width(7)) comparator_10 (.a(inst[6:0]), .b(7'b0100011), .eq(mem_w_en));  // open: gt, lt
  Comparator #(.width(7)) comparator_11 (.a(inst[6:0]), .b(7'b1100011), .eq(B_type));  // open: gt, lt
  Comparator #(.width(7)) comparator_12 (.a(inst[6:0]), .b(7'b1101111), .eq(J_type));  // open: gt, lt
  Comparator #(.width(7)) comparator_13 (.a(inst[6:0]), .b(7'b1100111), .eq(I_jalr));  // open: gt, lt
  Comparator #(.width(7)) comparator_14 (.a(inst[6:0]), .b(7'b0110111), .eq(U_lui));  // open: gt, lt
  Comparator #(.width(7)) comparator_15 (.a(inst[6:0]), .b(7'b0010111), .eq(U_type_AUIPC));  // open: gt, lt
  Comparator #(.width(3)) comparator_16 (.a(inst[14:12]), .b(3'b000), .eq(comparator_16_eq));  // open: gt, lt
  Comparator #(.width(7)) comparator_17 (.a(inst[31:25]), .b({7{1'b0}}), .eq(comparator_17_eq));  // open: gt, lt
  Comparator #(.width(3)) comparator_18 (.a(inst[14:12]), .b(3'b000), .eq(comparator_18_eq));  // open: gt, lt
  Comparator #(.width(7)) comparator_19 (.a(inst[31:25]), .b(7'b0000001), .eq(comparator_19_eq));  // open: gt, lt
  Comparator #(.width(3)) comparator_20 (.a(inst[14:12]), .b(3'b000), .eq(comparator_20_eq));  // open: gt, lt
  Comparator #(.width(7)) comparator_21 (.a(inst[31:25]), .b(7'b0100000), .eq(comparator_21_eq));  // open: gt, lt
  Comparator #(.width(3)) comparator_22 (.a(inst[14:12]), .b(3'b001), .eq(comparator_22_eq));  // open: gt, lt
  Comparator #(.width(7)) comparator_23 (.a(inst[31:25]), .b({7{1'b0}}), .eq(comparator_23_eq));  // open: gt, lt
  Comparator #(.width(3)) comparator_24 (.a(inst[14:12]), .b(3'b001), .eq(comparator_24_eq));  // open: gt, lt
  Comparator #(.width(7)) comparator_25 (.a(inst[31:25]), .b(7'b0000001), .eq(comparator_25_eq));  // open: gt, lt
  Comparator #(.width(3)) comparator_26 (.a(inst[14:12]), .b(3'b010), .eq(comparator_26_eq));  // open: gt, lt
  Comparator #(.width(7)) comparator_27 (.a(inst[31:25]), .b({7{1'b0}}), .eq(comparator_27_eq));  // open: gt, lt
  and and_7 (R_add, R_type, comparator_16_eq, comparator_17_eq);
  and and_8 (R_mul, R_type, comparator_18_eq, comparator_19_eq);
  and and_9 (R_sub, R_type, comparator_20_eq, comparator_21_eq);
  and and_10 (R_sll, R_type, comparator_22_eq, comparator_23_eq);
  and and_11 (R_mulh, R_type, comparator_24_eq, comparator_25_eq);
  and and_12 (R_slt, R_type, comparator_26_eq, comparator_27_eq);
  Comparator #(.width(3)) comparator_28 (.a(inst[14:12]), .b(3'b100), .eq(comparator_28_eq));  // open: gt, lt
  Comparator #(.width(7)) comparator_29 (.a(inst[31:25]), .b({7{1'b0}}), .eq(comparator_29_eq));  // open: gt, lt
  Comparator #(.width(3)) comparator_30 (.a(inst[14:12]), .b(3'b100), .eq(comparator_30_eq));  // open: gt, lt
  Comparator #(.width(7)) comparator_31 (.a(inst[31:25]), .b(7'b0000001), .eq(comparator_31_eq));  // open: gt, lt
  Comparator #(.width(3)) comparator_32 (.a(inst[14:12]), .b(3'b101), .eq(comparator_32_eq));  // open: gt, lt
  Comparator #(.width(7)) comparator_33 (.a(inst[31:25]), .b({7{1'b0}}), .eq(comparator_33_eq));  // open: gt, lt
  Comparator #(.width(3)) comparator_34 (.a(inst[14:12]), .b(3'b110), .eq(comparator_34_eq));  // open: gt, lt
  Comparator #(.width(7)) comparator_35 (.a(inst[31:25]), .b({7{1'b0}}), .eq(comparator_35_eq));  // open: gt, lt
  Comparator #(.width(3)) comparator_36 (.a(inst[14:12]), .b(3'b110), .eq(comparator_36_eq));  // open: gt, lt
  Comparator #(.width(7)) comparator_37 (.a(inst[31:25]), .b(7'b0000001), .eq(comparator_37_eq));  // open: gt, lt
  Comparator #(.width(3)) comparator_38 (.a(inst[14:12]), .b(3'b111), .eq(comparator_38_eq));  // open: gt, lt
  Comparator #(.width(7)) comparator_39 (.a(inst[31:25]), .b({7{1'b0}}), .eq(comparator_39_eq));  // open: gt, lt
  and and_13 (R_xor, R_type, comparator_28_eq, comparator_29_eq);
  and and_14 (R_div, R_type, comparator_30_eq, comparator_31_eq);
  and and_15 (R_srl, R_type, comparator_32_eq, comparator_33_eq);
  and and_16 (R_or, R_type, comparator_34_eq, comparator_35_eq);
  and and_17 (R_rem, R_type, comparator_36_eq, comparator_37_eq);
  and and_18 (R_and, R_type, comparator_38_eq, comparator_39_eq);
  Comparator #(.width(3)) comparator_40 (.a(inst[14:12]), .b(3'b000), .eq(comparator_40_eq));  // open: gt, lt
  Comparator #(.width(3)) comparator_41 (.a(inst[14:12]), .b(3'b001), .eq(comparator_41_eq));  // open: gt, lt
  Comparator #(.width(3)) comparator_42 (.a(inst[14:12]), .b(3'b010), .eq(comparator_42_eq));  // open: gt, lt
  and and_19 (I_lb, I_type_load, comparator_40_eq);
  and and_20 (I_lh, I_type_load, comparator_41_eq);
  and and_21 (I_lw, I_type_load, comparator_42_eq);
  Comparator #(.width(3)) comparator_43 (.a(inst[14:12]), .b(3'b000), .eq(comparator_43_eq));  // open: gt, lt
  Comparator #(.width(7)) comparator_44 (.a(inst[31:25]), .b({7{1'b0}}), .eq(comparator_44_eq));  // open: gt, lt
  Comparator #(.width(3)) comparator_45 (.a(inst[14:12]), .b(3'b001), .eq(comparator_45_eq));  // open: gt, lt
  Comparator #(.width(7)) comparator_46 (.a(inst[31:25]), .b({7{1'b0}}), .eq(comparator_46_eq));  // open: gt, lt
  Comparator #(.width(3)) comparator_47 (.a(inst[14:12]), .b(3'b010), .eq(comparator_47_eq));  // open: gt, lt
  Comparator #(.width(7)) comparator_48 (.a(inst[31:25]), .b({7{1'b0}}), .eq(comparator_48_eq));  // open: gt, lt
  Comparator #(.width(3)) comparator_49 (.a(inst[14:12]), .b(3'b100), .eq(comparator_49_eq));  // open: gt, lt
  Comparator #(.width(7)) comparator_50 (.a(inst[31:25]), .b({7{1'b0}}), .eq(comparator_50_eq));  // open: gt, lt
  Comparator #(.width(3)) comparator_51 (.a(inst[14:12]), .b(3'b101), .eq(comparator_51_eq));  // open: gt, lt
  Comparator #(.width(7)) comparator_52 (.a(inst[31:25]), .b({7{1'b0}}), .eq(comparator_52_eq));  // open: gt, lt
  and and_22 (I_add, I_type_arith, comparator_43_eq, comparator_44_eq);
  and and_23 (I_sll, I_type_arith, comparator_45_eq, comparator_46_eq);
  and and_24 (I_slt, I_type_arith, comparator_47_eq, comparator_48_eq);
  and and_25 (I_xor, I_type_arith, comparator_49_eq, comparator_50_eq);
  and and_26 (I_srl, I_type_arith, comparator_51_eq, comparator_52_eq);
  Comparator #(.width(3)) comparator_53 (.a(inst[14:12]), .b(3'b110), .eq(comparator_53_eq));  // open: gt, lt
  Comparator #(.width(7)) comparator_54 (.a(inst[31:25]), .b({7{1'b0}}), .eq(comparator_54_eq));  // open: gt, lt
  Comparator #(.width(3)) comparator_55 (.a(inst[14:12]), .b(3'b111), .eq(comparator_55_eq));  // open: gt, lt
  Comparator #(.width(7)) comparator_56 (.a(inst[31:25]), .b({7{1'b0}}), .eq(comparator_56_eq));  // open: gt, lt
  and and_27 (I_or, I_type_arith, comparator_53_eq, comparator_54_eq);
  and and_28 (I_and, I_type_arith, comparator_55_eq, comparator_56_eq);
  Comparator #(.width(3)) comparator_57 (.a(inst[14:12]), .b(3'b010), .eq(comparator_57_eq));  // open: gt, lt
  Comparator #(.width(3)) comparator_58 (.a(inst[14:12]), .b(3'b000), .eq(comparator_58_eq));  // open: gt, lt
  Comparator #(.width(3)) comparator_59 (.a(inst[14:12]), .b(3'b001), .eq(comparator_59_eq));  // open: gt, lt
  Comparator #(.width(3)) comparator_60 (.a(inst[14:12]), .b(3'b100), .eq(comparator_60_eq));  // open: gt, lt
  Comparator #(.width(3)) comparator_61 (.a(inst[14:12]), .b(3'b101), .eq(comparator_61_eq));  // open: gt, lt
  Comparator #(.width(3)) comparator_62 (.a(inst[14:12]), .b(3'b110), .eq(comparator_62_eq));  // open: gt, lt
  Comparator #(.width(3)) comparator_63 (.a(inst[14:12]), .b(3'b111), .eq(comparator_63_eq));  // open: gt, lt
  and and_29 (S_sw, mem_w_en, comparator_57_eq);
  and and_30 (B_beq, B_type, comparator_58_eq);
  and and_31 (B_bne, B_type, comparator_59_eq);
  and and_32 (B_blt, B_type, comparator_60_eq);
  and and_33 (B_bge, B_type, comparator_61_eq);
  and and_34 (B_bltu, B_type, comparator_62_eq);
  and and_35 (B_bgeu, B_type, comparator_63_eq);

  // Other names for the same wires on the sheet: rd_idx[4:0] = inst[11:7]; r2_idx[4:0] = inst[24:20];
  //   funct7[6:0] = inst[31:25]; funct3[2:0] = inst[14:12]; r1_idx[4:0] = inst[19:15]; alu_out[31:0] = mem_addr;
  //   I_type_jump = I_jalr; opcode[6:0] = inst[6:0]; r2_data[31:0] = mem_write_data; S_type = mem_w_en;
  //   U_jal = J_type; U_type_load = U_lui

  // Notes on the sheet:
  //   I/O
  //   1.Fetch
  //   2.DECODE
  //   3. Registers
  //   4. Execute
  //   R-Type
  //   I-Type
  //   S-Type
  //   B-Type
  //   U-Type
  //   J-Type
  //   5. Writeback
  //   instRUCTION Parameterization
  //   imm[11:0]
  //   imm[4:0]
  //   imm[11:5]
  //   imm[11]
  //   imm[4:1]
  //   imm[10:5]
  //   imm[12]
  //   imm[31:12]
  //   imm[19:12]
  //   imm[11]
  //   imm[10:1]
  //   imm[20]
  //   Outputs
  //   Inputs
  //   instRUCTION DECODING
endmodule

module RegFile (
  input  [4:0] reg_read_idx1,
  input  [4:0] reg_read_idx2,
  input  [4:0] reg_w_idx,
  input  [31:0] reg_write_data,
  input  reg_w_en,
  input  clk,
  output [31:0] RegReadData1,
  output [31:0] RegReadData2,
  output [31:0] reg_gp
);

  wire we_1, we_2, we_3, we_4, we_5, we_6, we_7, we_8, we_9, we_10, we_11, we_12, we_13, we_14, we_15, we_16,
       we_17, we_18, we_19, we_20, we_21, we_22, we_23, we_24, we_25, we_26, we_27, we_28, we_29, we_30,
       we_31;
  wire [31:0] in_x1, in_x2, in_x3, in_x4, in_x5, in_x6, in_x7, in_x8, in_x9, in_x10, in_x11, in_x12, in_x13,
       in_x14, in_x15, in_x16, in_x17, in_x18, in_x19, in_x20, in_x21, in_x22, in_x23, in_x24, in_x25,
       in_x26, in_x27, in_x28, in_x29, in_x30, in_x31, out_x1, out_x2, out_x4, out_x5, out_x6, out_x7,
       out_x8, out_x9, out_x10, out_x11, out_x12, out_x13, out_x14, out_x15, out_x16, out_x17, out_x18,
       out_x19, out_x20, out_x21, out_x22, out_x23, out_x24, out_x25, out_x26, out_x27, out_x28, out_x29,
       out_x30, out_x31;

  Register #(.width(32)) register_1 (.D(in_x1), .en(we_1), .clk(clk), .Q(out_x1));  // open: clr
  Register #(.width(32)) register_2 (.D(in_x9), .en(we_9), .clk(clk), .Q(out_x9));  // open: clr
  Register #(.width(32)) register_3 (.D(in_x17), .en(we_17), .clk(clk), .Q(out_x17));  // open: clr
  Register #(.width(32)) register_4 (.D(in_x25), .en(we_25), .clk(clk), .Q(out_x25));  // open: clr
  Multiplexer #(.select(5), .width(32)) multiplexer_1 (
    .in0({32{1'b0}}), .in1(out_x1), .in2(out_x2), .in3(reg_gp), .in4(out_x4), .in5(out_x5), .in6(out_x6),
    .in7(out_x7), .in8(out_x8), .in9(out_x9), .in10(out_x10), .in11(out_x11), .in12(out_x12), .in13(out_x13),
    .in14(out_x14), .in15(out_x15), .in16(out_x16), .in17(out_x17), .in18(out_x18), .in19(out_x19),
    .in20(out_x20), .in21(out_x21), .in22(out_x22), .in23(out_x23), .in24(out_x24), .in25(out_x25),
    .in26(out_x26), .in27(out_x27), .in28(out_x28), .in29(out_x29), .in30(out_x30), .in31(out_x31),
    .out(RegReadData1), .sel(reg_read_idx1));
  Register #(.width(32)) register_5 (.D(in_x2), .en(we_2), .clk(clk), .Q(out_x2));  // open: clr
  Register #(.width(32)) register_6 (.D(in_x10), .en(we_10), .clk(clk), .Q(out_x10));  // open: clr
  Register #(.width(32)) register_7 (.D(in_x18), .en(we_18), .clk(clk), .Q(out_x18));  // open: clr
  Register #(.width(32)) register_8 (.D(in_x26), .en(we_26), .clk(clk), .Q(out_x26));  // open: clr
  Register #(.width(32)) register_9 (.D(in_x3), .en(we_3), .clk(clk), .Q(reg_gp));  // open: clr
  Register #(.width(32)) register_10 (.D(in_x11), .en(we_11), .clk(clk), .Q(out_x11));  // open: clr
  Register #(.width(32)) register_11 (.D(in_x19), .en(we_19), .clk(clk), .Q(out_x19));  // open: clr
  Register #(.width(32)) register_12 (.D(in_x27), .en(we_27), .clk(clk), .Q(out_x27));  // open: clr
  Multiplexer #(.select(5), .width(32)) multiplexer_2 (
    .in0({32{1'b0}}), .in1(out_x1), .in2(out_x2), .in3(reg_gp), .in4(out_x4), .in5(out_x5), .in6(out_x6),
    .in7(out_x7), .in8(out_x8), .in9(out_x9), .in10(out_x10), .in11(out_x11), .in12(out_x12), .in13(out_x13),
    .in14(out_x14), .in15(out_x15), .in16(out_x16), .in17(out_x17), .in18(out_x18), .in19(out_x19),
    .in20(out_x20), .in21(out_x21), .in22(out_x22), .in23(out_x23), .in24(out_x24), .in25(out_x25),
    .in26(out_x26), .in27(out_x27), .in28(out_x28), .in29(out_x29), .in30(out_x30), .in31(out_x31),
    .out(RegReadData2), .sel(reg_read_idx2));
  Register #(.width(32)) register_13 (.D(in_x4), .en(we_4), .clk(clk), .Q(out_x4));  // open: clr
  Register #(.width(32)) register_14 (.D(in_x12), .en(we_12), .clk(clk), .Q(out_x12));  // open: clr
  Register #(.width(32)) register_15 (.D(in_x20), .en(we_20), .clk(clk), .Q(out_x20));  // open: clr
  Register #(.width(32)) register_16 (.D(in_x28), .en(we_28), .clk(clk), .Q(out_x28));  // open: clr
  Demultiplexer #(.enable("true"), .select(5), .width(32)) demultiplexer_1 (
    .out1(in_x1), .out2(in_x2), .out3(in_x3), .out4(in_x4), .out5(in_x5), .out6(in_x6), .out7(in_x7),
    .out8(in_x8), .out9(in_x9), .out10(in_x10), .out11(in_x11), .out12(in_x12), .out13(in_x13),
    .out14(in_x14), .out15(in_x15), .out16(in_x16), .out17(in_x17), .out18(in_x18), .out19(in_x19),
    .out20(in_x20), .out21(in_x21), .out22(in_x22), .out23(in_x23), .out24(in_x24), .out25(in_x25),
    .out26(in_x26), .out27(in_x27), .out28(in_x28), .out29(in_x29), .out30(in_x30), .out31(in_x31),
    .in(reg_write_data), .sel(reg_w_idx), .en(reg_w_en));  // open: out0
  Register #(.width(32)) register_17 (.D(in_x5), .en(we_5), .clk(clk), .Q(out_x5));  // open: clr
  Register #(.width(32)) register_18 (.D(in_x13), .en(we_13), .clk(clk), .Q(out_x13));  // open: clr
  Register #(.width(32)) register_19 (.D(in_x21), .en(we_21), .clk(clk), .Q(out_x21));  // open: clr
  Register #(.width(32)) register_20 (.D(in_x29), .en(we_29), .clk(clk), .Q(out_x29));  // open: clr
  Register #(.width(32)) register_21 (.D(in_x6), .en(we_6), .clk(clk), .Q(out_x6));  // open: clr
  Register #(.width(32)) register_22 (.D(in_x14), .en(we_14), .clk(clk), .Q(out_x14));  // open: clr
  Register #(.width(32)) register_23 (.D(in_x22), .en(we_22), .clk(clk), .Q(out_x22));  // open: clr
  Register #(.width(32)) register_24 (.D(in_x30), .en(we_30), .clk(clk), .Q(out_x30));  // open: clr
  Decoder #(.select(5)) decoder_1 (
    .out1(we_1), .out2(we_2), .out3(we_3), .out4(we_4), .out5(we_5), .out6(we_6), .out7(we_7), .out8(we_8),
    .out9(we_9), .out10(we_10), .out11(we_11), .out12(we_12), .out13(we_13), .out14(we_14), .out15(we_15),
    .out16(we_16), .out17(we_17), .out18(we_18), .out19(we_19), .out20(we_20), .out21(we_21), .out22(we_22),
    .out23(we_23), .out24(we_24), .out25(we_25), .out26(we_26), .out27(we_27), .out28(we_28), .out29(we_29),
    .out30(we_30), .out31(we_31), .sel(reg_w_idx), .en(reg_w_en));  // open: out0
  Register #(.width(32)) register_25 (.D(in_x7), .en(we_7), .clk(clk), .Q(out_x7));  // open: clr
  Register #(.width(32)) register_26 (.D(in_x15), .en(we_15), .clk(clk), .Q(out_x15));  // open: clr
  Register #(.width(32)) register_27 (.D(in_x23), .en(we_23), .clk(clk), .Q(out_x23));  // open: clr
  Register #(.width(32)) register_28 (.D(in_x31), .en(we_31), .clk(clk), .Q(out_x31));  // open: clr
  Register #(.width(32)) register_29 (.D(in_x8), .en(we_8), .clk(clk), .Q(out_x8));  // open: clr
  Register #(.width(32)) register_30 (.D(in_x16), .en(we_16), .clk(clk), .Q(out_x16));  // open: clr
  Register #(.width(32)) register_31 (.D(in_x24), .en(we_24), .clk(clk), .Q(out_x24));  // open: clr

  // Other names for the same wires on the sheet: out_x3[31:0] = reg_gp

  // Notes on the sheet:
  //   Outputs
  //   Register Reading
  //   I/O
  //   Inputs
  //   Register Writing
endmodule

module ALU (
  input  [31:0] A,
  input  [31:0] B,
  input  [3:0] OP,
  output [31:0] C
);

  wire comparator_1_lt;
  wire [31:0] adder_1_out, and_1_out, bit_extender_1_out, divider_1_out, divider_2_rem, multiplier_1_out,
       multiplier_2_cout, or_1_out, shifter_1_out, shifter_2_out, subtractor_1_out, xor_1_out;

  Adder #(.width(32)) adder_1 (.a(A), .b(B), .out(adder_1_out));  // open: cin, cout
  Subtractor #(.width(32)) subtractor_1 (.a(A), .b(B), .out(subtractor_1_out));  // open: bin, bout
  assign and_1_out = A & B;  // AND_Gate and_1, 32 bits wide
  assign or_1_out = A | B;  // OR_Gate or_1, 32 bits wide
  assign xor_1_out = A ^ B;  // XOR_Gate xor_1, 32 bits wide
  Shifter #(.width(32)) shifter_1 (.in(A), .\dist (B[4:0]), .out(shifter_1_out));
  Shifter #(.shift("lr"), .width(32)) shifter_2 (.in(A), .\dist (B[4:0]), .out(shifter_2_out));
  Multiplier #(.width(32)) multiplier_1 (.a(A), .b(B), .out(multiplier_1_out));  // open: cin, cout
  Multiplier #(.width(32)) multiplier_2 (.a(A), .b(B), .cout(multiplier_2_cout));  // open: out, cin
  Divider #(.width(32)) divider_1 (.a(A), .b(B), .out(divider_1_out));  // open: upper, rem
  Divider #(.width(32)) divider_2 (.a(A), .b(B), .rem(divider_2_rem));  // open: out, upper
  Bit_Extender #(.in_width(1), .out_width(32)) bit_extender_1 (.out(bit_extender_1_out));  // open: in
  Comparator #(.width(32)) comparator_1 (.a(A), .b(B), .lt(comparator_1_lt));  // open: gt, eq
  Multiplexer #(.select(4), .width(32)) multiplexer_1 (
    .in0(adder_1_out), .in1(subtractor_1_out), .in2(and_1_out), .in3(or_1_out), .in4(xor_1_out),
    .in5(shifter_1_out), .in6(shifter_2_out), .in7(multiplier_1_out), .in8(multiplier_2_cout),
    .in9(divider_1_out), .in10(divider_2_rem), .in11(bit_extender_1_out), .out(C), .sel(OP));  // open: in12, in13, in14, in15

  // Notes on the sheet:
  //   add
  //   sub
  //   and
  //   or
  //   xor
  //   sll
  //   srl
  //   mul
  //   mulh
  //   div
  //   rem
  //   slt
  //   Outputs
  //   I/O
  //   Inputs
endmodule

module main (
);

  wire clk, cpu_1_mem_w_en, not_1_out;
  wire [31:0] cpu_1_mem_addr, cpu_1_mem_write_data, cpu_1_pc, cpu_1_reg_gp, IMEM_data, ram_1_dout,
       shifter_1_out, shifter_2_out;

  // Probe on cpu_1_mem_write_data
  // Probe on shifter_1_out[9:0]
  Shifter #(.shift("lr"), .width(32)) shifter_1 (.in(cpu_1_mem_addr), .\dist (5'b00010), .out(shifter_1_out));
  RAM #(.addrWidth(10), .asyncread("true"), .dataWidth(32)) ram_1 (
    .addr(shifter_1_out[9:0]), .we(cpu_1_mem_w_en), .oe(not_1_out), .clk(clk), .din(cpu_1_mem_write_data),
    .dout(ram_1_dout));
  not not_1 (not_1_out, cpu_1_mem_w_en);
  CPU cpu_1 (
    .mem_read_data(ram_1_dout), .inst(IMEM_data), .clk(clk), .mem_addr(cpu_1_mem_addr),
    .mem_write_data(cpu_1_mem_write_data), .mem_w_en(cpu_1_mem_w_en), .PC(cpu_1_pc), .reg_gp(cpu_1_reg_gp));
  // Probe on ram_1_dout
  Clock clock_1 (.out(clk));
  // Probe on cpu_1_reg_gp
  Shifter #(.shift("lr"), .width(32)) shifter_2 (.in(cpu_1_pc), .\dist (5'b00010), .out(shifter_2_out));
  ROM #(.addrWidth(10), .dataWidth(32)) IMEM (.addr(shifter_2_out[9:0]), .data(IMEM_data));

  // Notes on the sheet:
  //   RISC-V Computer (RV32IM)
  //   Emin FEDAR | 2020
  //   Modified by DaleyDeng | 2023
  //   contents of IMEM (hex, n*v repeats v):
  //   193 1000f6f 19463 10000193 6f 200193 93 113 208733 393 4c771663 300193 100093 100113 208733 200393
  //   4a771a63 400193 300093 700113 208733 a00393 48771e63 500193 93 ffff8137 208733 ffff83b7 48771263
  //   600193 800000b7 113 208733 800003b7 46771663 700193 800000b7 ffff8137 208733 7fff83b7 44771a63
  //   800193 93 8137 fff10113 208733 83b7 fff38393 42771a63 900193 800000b7 fff08093 113 208733 800003b7
  //   fff38393 40771a63 a00193 800000b7 fff08093 8137 fff10113 208733 800083b7 ffe38393 3e771863 b00193
  //   800000b7 8137 fff10113 208733 800083b7 fff38393 3c771863 c00193 800000b7 fff08093 ffff8137 208733
  //   7fff83b7 fff38393 3a771863 d00193 93 fff00113 208733 fff00393 38771c63 e00193 fff00093 100113 208733
  //   393 38771063 f00193 fff00093 fff00113 208733 ffe00393 36771463 1000193 100093 80000137 fff10113
  //   208733 800003b7 34771663 1100193 d00093 b00113 2080b3 1800393 32709a63 1200193 e00093 b00113 208133
  //   1900393 30711e63 1300193 d00093 1080b3 1a00393 30709463 1400193 213 d00093 b00113 208733 70313
  //   120213 200293 fe5214e3 1800393 2c731e63 1500193 213 e00093 b00113 208733 13 70313 120213 200293
  //   fe5212e3 1900393 2a731663 1600193 213 f00093 b00113 208733 13 13 70313 120213 200293 fe5210e3
  //   1a00393 26731c63 1700193 213 d00093 b00113 208733 120213 200293 fe5216e3 1800393 24771863 1800193
  //   213 e00093 b00113 13 208733 120213 200293 fe5214e3 1900393 22771263 1900193 213 f00093 b00113 13 13
  //   208733 120213 200293 fe5212e3 1a00393 1e771a63 1a00193 213 d00093 13 b00113 208733 120213 200293
  //   fe5214e3 1800393 1c771463 1b00193 213 e00093 13 b00113 13 208733 120213 200293 fe5212e3 1900393
  //   18771c63 1c00193 213 f00093 13 13 b00113 208733 120213 200293 fe5212e3 1a00393 16771463 1d00193 213
  //   b00113 d00093 208733 120213 200293 fe5216e3 1800393 14771063 1e00193 213 b00113 e00093 13 208733
  //   120213 200293 fe5214e3 1900393 10771a63 1f00193 213 b00113 f00093 13 13 208733 120213 200293
  //   fe5212e3 1a00393 e771263 2000193 213 b00113 13 d00093 208733 120213 200293 fe5214e3 1800393 a771c63
  //   2100193 213 b00113 13 e00093 13 208733 120213 200293 fe5212e3 1900393 8771463 2200193 213 b00113 13
  //   13 f00093 208733 120213 200293 fe5212e3 1a00393 4771c63 2300193 f00093 100133 f00393 4711263 2400193
  //   2000093 8133 2000393 2711863 2500193 b3 393 2709063 2600193 1000093 1e00113 208033 393 701463 193
  //   f0067
endmodule
